# Fritzing sketch test (saved by Fritzing 0.9.3b)
circuit board: 8.46667cm x 5.64444cm

parts:
  Part1 = Arduino Pro Mini (5V)
  R1 = Resistor [package="2512 [SMD]"]
  R2 = Resistor [package="2512 [SMD]"]
  R3 = Resistor [package="2512 [SMD]"]
  R4 = Resistor [package="2512 [SMD]"]
  R5 = Resistor [tolerance=±5% resistance=220 package=THT]
  Q2 = MOSFET-NCHANNEL [package=to220v]
  S1 = Pushbutton [package=THT]
  S2 = Pushbutton [package=THT]
  S3 = Pushbutton [package=THT]
  Part2 = OLED Monochrome 128x32 I2C [part_number=931]
  U1 = LIPO-2000mAh [package=lipo-2000]

nets:
  VCC: Part1.VCC, S1.leg0, S2.leg0, S3.leg0, Part2.VIN
  GND: Part1.GND, R2.Pin_1, R3.Pin_1, Q2.S, S1.leg1, S2.leg1, S3.leg1, Part2.GND, U1.-
  N1: Part1.A4, Part2.SDA
  N2: Part1.A5, Part2.SCL
  N3: Part1.RAW, U1.+
  N4: Part1.MISO, R2.Pin_0
  N5: Part1.MOSI, R3.Pin_0
  N6: Part1.D7, R4.Pin_0
  N7: Part1.D4, Part2.RESET
  N8: Part1.D3, R5.Pin_0
  N9: R1.Pin_0, R5.Pin_1, Q2.G

custom parts:
  Resistor: Resistor Basic schematic elements and footprints for 0603, 1206, and PTH resistors.
  OLED Monochrome 128x32 I2C: These displays are small, only about 1" diagonal, but very readable due to the high contrast of an OLED display. This display is made of 128x32 individual white OLED pixels, each one is turned on or off by the controller chip. Because the display makes its own light, no backlight is required. This reduces the power required to run the OLED and is why the display has such high contrast; we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
